# Fritzing sketch PoolButtler (saved by Fritzing 1.0.5)

parts:
  U2 = ESP8266 WiFi Module [part_number=ESP8266]
  S1 = PH meter [package=THT]
  DS1 = DS18B20 1-Wire Temperature Sensor [part_number=DS18B20]
  U3 = DFRobot SEN0189 [package=THT]
  U4 = Turbidity Sensor Probe [package=THT]
  A1 = Analog ORP Sensor
  RHT1 = Humidity and Temperature Sensor RHT03

nets:
  N1: U2.IO0, A1.Pin_3
  N2: U2.D2, RHT1.Data-signal
  N3: U2.D0, U3.P1_1
  N4: U2.D1, S1.pin1
  N5: U2.D3, DS1.DQ
  N6: U2.3.3V#10, A1.Pin_2
  N7: U2.GND#12, S1.pin3
  N8: U2.GND#13, DS1.GND
  N9: U2.GND#23, U3.P1_3, A1.Pin_1, RHT1.GND_2
  N10: U2.3.3V#26, U3.P1_2
  5V: S1.pin2, DS1.VDD, RHT1.Vcc
  N11: U3.P2_1, U4.pin1
  N12: U3.P2_2, U4.pin2
  N13: U3.P2_3, U4.VCC

custom parts:
  DFRobot SEN0189: Turbidity sensor of DFRobot SEN0189
  Turbidity Sensor Probe: Turbidity sensor probe to the DFRobot measure module.
  Analog ORP Sensor: This Analog ORP Meter is a highly compact ORP monitoring system.
